# Fritzing sketch hardware (saved by Fritzing 0.9.0b)
breadboards: 1

parts:
  R1 = Photocell (LDR) [package=THT]
  BeagleBone1 = BeagleBone Black
  R2 = Resistor [tolerance=±5% resistance=10k package="0603 [SMD]"]

nets:
  N1: R1.pin_0, BeagleBone1.no_name_yet#32
  N2: R1.pin_1, BeagleBone1.no_name_yet#40, R2.Pin_0
  N3: BeagleBone1.no_name_yet#34, R2.Pin_1

notes:
  LDR: 70..100K Ohm LDR VT90N2
  10K

custom parts:
  BeagleBone Black: BeagleBone Black rev. A5B
